# Fritzing sketch rgb_led_switch (saved by Fritzing 0.9.4)
breadboards: 1

parts:
  A2 = Particle Photon 2
  S2 = Toggle Switch [package=THT]

nets:
  N1: A2.Pin_2, S2.L1
  N2: A2.Pin_4, A2.Pin_30, S2.L2
  N3: A2.Pin_10, S2.COM
  N4: A2.Pin_28, A2.Pin_29

custom parts:
  Particle Photon 2: The Photon 2 is a development module with a microcontroller and Wi-Fi networking. -- This Fritzing file originally created by Peter Van Epp https://forum.fritzing.org/t/request-particle-photon2/19824/2 5/18/2024 - Rob Parke Rotated breadboard image
