# Fritzing sketch car_lipo_hookup_no_wires (saved by Fritzing 0.9.10b)

parts:
  U2 = LIPO-2000mAh [package=lipo-2000]
  J2 = JST-03JQ-BT [part_number=JST-JQ-BT package=THT]
  A1 = Particle Photon 2  # not connected

nets:
  N1: U2.+, J2.pin3
  N2: U2.-, J2.pin2

notes:
  White LiPo connector plugs in to black Photon 2 battery port

custom parts:
  Particle Photon 2: The Photon 2 is a development module with a microcontroller and Wi-Fi networking. -- This Fritzing file originally created by Peter Van Epp https://forum.fritzing.org/t/request-particle-photon2/19824/2 5/18/2024 - Rob Parke Rotated breadboard image
