# Fritzing sketch accelerometer (saved by Fritzing 0.9.10b)
breadboards: 1

parts:
  Part1 = Triple Axis Accelerometer Breakout - ADXL345
  A1 = Particle Photon 2

nets:
  N1: Part1.GND, Part1.SDO, A1.Pin_4, A1.Pin_30, A1.Pin_35
  N2: Part1.VCC, Part1.CS, A1.Pin_2
  N3: Part1.SDA, A1.Pin_17
  N4: Part1.SCL, A1.Pin_18
  N5: A1.Pin_28, A1.Pin_29

custom parts:
  Particle Photon 2: The Photon 2 is a development module with a microcontroller and Wi-Fi networking. -- This Fritzing file originally created by Peter Van Epp https://forum.fritzing.org/t/request-particle-photon2/19824/2 5/18/2024 - Rob Parke Rotated breadboard image
