# Fritzing sketch accelerometer_rgb_led (saved by Fritzing 0.9.4)
breadboards: 1

parts:
  Argon1 = Particle Argon
  R9 = Resistor [tolerance=±5% resistance=330 package=THT]
  R10 = Resistor [tolerance=±5% resistance=330 package=THT]
  R11 = Resistor [tolerance=±5% resistance=330 package=THT]
  LED3 = RGB LED (com. cathode, rgb) [package="5 mm [THT]"]
  3-Axis_Accelerometer3 = 3-Axis Accelerometer Breakout - MMA8452Q  # not connected

nets:
  N1: Argon1.GND, LED3.common_cathode
  N2: Argon1.A3, R11.Pin_1
  N3: Argon1.A4, R10.Pin_1
  N4: Argon1.A5, R9.Pin_1
  N5: R9.Pin_0, LED3.red_anode
  N6: R10.Pin_0, LED3.green_anode
  N7: R11.Pin_0, LED3.blue_anode

custom parts:
  Particle Argon: The Argon is a powerful Wi-Fi enabled development board that can act as either a standalone Wi-Fi endpoint or Wi-Fi enabled gateway for Particle Mesh networks. It is based on the Nordic nRF52840 and has built-in battery charging circuitry so it’s easy to connect a Li-Po and deploy your local network in minutes. The Argon is great for connecting existing projects to the Particle Device Cloud or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
